# Fritzing sketch ESP32withPotButtonPhoto (saved by Fritzing 1.0.1rc)
breadboards: 1

parts:
  Part1 = Adafruit HUZZAH32 ESP32 Feather [part_number="Adafruit #3405"]
  POT1 = Breadboard Trimpot
  S1 = Momentary Switch [package=ksa_sealed_tac_switch]
  R2 = Resistor [tolerance=±5% power=0.25W resistance=10k package=THT]
  R3 = Resistor [tolerance=±5% power=0.25W resistance=10k package=THT]
  R4 = Photocell (LDR) [power=0.25W dark_resistance_@0.01lx=300kΩ light_resistance_@100lx=400Ω luminance=10lx package=THT]

nets:
  N1: Part1.A3_I39, R3.Pin_0, R4.pin_1
  N2: Part1.A2_I34, POT1.PIN2
  N3: Part1.GND, POT1.PIN3, R2.Pin_1, R3.Pin_1
  N4: Part1.3.3V, POT1.PIN1, S1.4, R4.pin_0
  N5: Part1.IO13_A12, S1.2, R2.Pin_0
